// Logisim project Shmerlard8.circ as structural Verilog: 11 circuits, main circuit main
module main (
  input  RST,
  input  [15:0] in_2,
  input  MAN,
  input  in_4,
  input  in_5,
  input  in_6,
  input  in_7,
  input  in_8,
  input  in_9,
  input  in_10,
  input  [3:0] in_11,
  input  in_12,
  input  in_13,
  input  in_14,
  input  in_15,
  input  in_16,
  input  in_17,
  input  in_18,
  input  in_19,
  input  in_20,
  input  in_21,
  input  in_22,
  output [4:0] OPCODE,
  output [1:0] IR_ADD_DST,
  output [2:0] IR_ADD_SRC
);

  wire CLK, memory_registers_1_ram_wr_en;
  wire [3:0] instruction_register_1_reg_sel_dst, instruction_register_1_reg_sel_src;
  wire [15:0] MANUAL, memory_registers_1_mem_address_out, memory_registers_1_mem_data_out;

  Clock u_CLK (.out(CLK));
  assign MANUAL = MAN ? in_2 : 16'bz;  // Controlled_Buffer controlled_buffer_1
  // Probe on instruction_register_1_reg_sel_src
  // Probe on instruction_register_1_reg_sel_dst
  program_counter program_counter_1 (
    .CLK(CLK), .RST(RST), .PC_OUT(in_6), .PC_IN(in_4), .PC_INC(in_8), .D_BUS(MANUAL), .D_BUS_OUT(MANUAL));
  instruction_register instruction_register_1 (
    .CLK(CLK), .IR_OUT(in_12), .D_BUS(MANUAL), .IR_WR_EN(in_14), .RST(RST),
    .REG_SEL_DST(instruction_register_1_reg_sel_dst), .ADDR_MODE(IR_ADD_SRC),
    .REG_SEL_SRC(instruction_register_1_reg_sel_src), .OP_CODE(OPCODE), .D_BUS_OUT(MANUAL));
  register_file register_file_1 (
    .src_DST(in_20), .REG_WR(in_18), .REG_RD(in_16), .REG_SEL_SRC(instruction_register_1_reg_sel_src),
    .REG_SEL_DST(instruction_register_1_reg_sel_dst), .CLK(CLK), .RST(RST), .DATA_IN(MANUAL),
    .DATA_OUT(MANUAL));  // open: RF_FL_IN, FLAGS_OUT
  z74_alu z74_alu_1 (
    .Y_OUT(in_9), .Y_IN(in_7), .RST(RST), .CLK(CLK), .X_in(in_5), .DATAIN(MANUAL), .S_in(in_11),
    .M_in(in_13), .Cin(in_10), .Y_DATA_OUT(MANUAL));  // open: A_EQ_B, C_out
  // Probe on MANUAL
  memory_registers memory_registers_1 (
    .D_BUS(MANUAL), .MAR_WR_EN(in_15), .MDR_WR_EN(in_19), .MEM_sel(in_21), .WR_sel(in_22),
    .MDR_OUT_EN(in_17), .CLK(CLK), .RST(RST), .MEM_DATA_IN(memory_registers_1_mem_data_out),
    .MEM_ADDRESS_OUT(memory_registers_1_mem_address_out), .D_BUS_OUT(MANUAL),
    .MEM_DATA_OUT(memory_registers_1_mem_data_out), .RAM_WR_EN(memory_registers_1_ram_wr_en));

  // Other names for the same wires on the sheet: ALU_C_In = in_10; ALU_M = in_13; ALU_S[3:0] = in_11; DSTsel = in_20;
  //   IR_IN = in_14; IR_OUT = in_12; MAR_IN = in_15; MDR_IN = in_19; MDR_OUT = in_17; MEM_SEL = in_21; PC_IN = in_4;
  //   PC_INC = in_8; PC_OUT = in_6; RF_IN = in_18; RF_OUT = in_16; WR_SEL = in_22; X_IN = in_5; Y_IN = in_7;
  //   Y_OUT = in_9
endmodule

module register_file (
  input  CLK,
  input  RST,
  input  RF_FL_IN,
  input  [15:0] DATA_IN,
  input  REG_WR,
  input  [3:0] REG_SEL_SRC,
  input  [3:0] REG_SEL_DST,
  input  src_DST,
  input  REG_RD,
  output [15:0] DATA_OUT,
  output [3:0] FLAGS_OUT
);

  wire decoder_1_out1, not_1_out, RD_EN_C, RD_EN_D, RD_EN_E, RD_EN_F, RD_EN_REG2, RD_EN_REG3, RD_EN_SP,
       RD_EN_SR, WR_EN_C, WR_EN_D, WR_EN_E, WR_EN_F, WR_EN_REG2, WR_EN_REG3, WR_EN_SP, WR_EN_SR;
  wire [3:0] multiplexer_1_out;
  wire [15:0] C_REG_q, D_REG_q, E_REG_q, F_REG_q, REG2_q, REG3_q, SP_REG_q;
  wire [15:4] STATUS_REG_q;

  Hex_Digit_Display hex_digit_display_1 (.value(REG_SEL_DST));  // open: dp
  Hex_Digit_Display hex_digit_display_2 (.value(REG_SEL_SRC));  // open: dp
  LED led_1 (.in(not_1_out));
  not not_1 (not_1_out, src_DST);
  LED led_2 (.in(src_DST));
  Multiplexer #(.width(4)) multiplexer_1 (.in0(REG_SEL_SRC), .in1(REG_SEL_DST), .out(multiplexer_1_out), .sel(src_DST));
  // Probe on multiplexer_1_out
  Decoder #(.select(4)) decoder_1 (
    .out0(WR_EN_SP), .out1(decoder_1_out1), .out2(WR_EN_REG2), .out3(WR_EN_REG3), .out4(WR_EN_C),
    .out5(WR_EN_D), .out6(WR_EN_E), .out7(WR_EN_F), .sel(multiplexer_1_out), .en(REG_WR));  // open: out8, out9, out10, out11, out12, out13, out14, out15
  Decoder #(.select(4)) decoder_2 (
    .out0(RD_EN_SP), .out1(RD_EN_SR), .out2(RD_EN_REG2), .out3(RD_EN_REG3), .out4(RD_EN_C), .out5(RD_EN_D),
    .out6(RD_EN_E), .out7(RD_EN_F), .sel(multiplexer_1_out), .en(REG_RD));  // open: out8, out9, out10, out11, out12, out13, out14, out15
  or or_1 (WR_EN_SR, RF_FL_IN, decoder_1_out1);
  Register #(.width(16)) SP_REG (.D(DATA_IN), .en(WR_EN_SP), .clk(CLK), .Q(SP_REG_q), .clr(RST));
  Register #(.width(16)) STATUS_REG (.D(DATA_IN), .en(WR_EN_SR), .clk(CLK), .Q({STATUS_REG_q, FLAGS_OUT}), .clr(RST));
  Register #(.width(16)) REG2 (.D(DATA_IN), .en(WR_EN_REG2), .clk(CLK), .Q(REG2_q), .clr(RST));
  Register #(.width(16)) REG3 (.D(DATA_IN), .en(WR_EN_REG3), .clk(CLK), .Q(REG3_q), .clr(RST));
  Register #(.width(16)) C_REG (.D(DATA_IN), .en(WR_EN_C), .clk(CLK), .Q(C_REG_q), .clr(RST));
  Register #(.width(16)) D_REG (.D(DATA_IN), .en(WR_EN_D), .clk(CLK), .Q(D_REG_q), .clr(RST));
  Register #(.width(16)) E_REG (.D(DATA_IN), .en(WR_EN_E), .clk(CLK), .Q(E_REG_q), .clr(RST));
  Register #(.width(16)) F_REG (.D(DATA_IN), .en(WR_EN_F), .clk(CLK), .Q(F_REG_q), .clr(RST));
  assign DATA_OUT = RD_EN_SP ? SP_REG_q : 16'bz;  // Controlled_Buffer controlled_buffer_1
  assign DATA_OUT = RD_EN_SR ? {STATUS_REG_q, FLAGS_OUT} : 16'bz;  // Controlled_Buffer controlled_buffer_2
  assign DATA_OUT = RD_EN_REG2 ? REG2_q : 16'bz;  // Controlled_Buffer controlled_buffer_3
  assign DATA_OUT = RD_EN_REG3 ? REG3_q : 16'bz;  // Controlled_Buffer controlled_buffer_4
  assign DATA_OUT = RD_EN_C ? C_REG_q : 16'bz;  // Controlled_Buffer controlled_buffer_5
  assign DATA_OUT = RD_EN_D ? D_REG_q : 16'bz;  // Controlled_Buffer controlled_buffer_6
  assign DATA_OUT = RD_EN_E ? E_REG_q : 16'bz;  // Controlled_Buffer controlled_buffer_7
  assign DATA_OUT = RD_EN_F ? F_REG_q : 16'bz;  // Controlled_Buffer controlled_buffer_8
endmodule

module instruction_register (
  input  CLK,
  input  RST,
  input  IR_OUT,
  input  [15:0] D_BUS,
  input  IR_WR_EN,
  output [15:0] D_BUS_OUT,
  output [3:0] REG_SEL_DST,
  output [2:0] ADDR_MODE,
  output [3:0] REG_SEL_SRC,
  output [4:0] OP_CODE
);

  Register #(.width(16)) IR (
    .D(D_BUS), .en(IR_WR_EN), .clk(CLK), .Q({OP_CODE, REG_SEL_SRC, ADDR_MODE, REG_SEL_DST}), .clr(RST));
  assign D_BUS_OUT = IR_OUT ? {OP_CODE, REG_SEL_SRC, ADDR_MODE, REG_SEL_DST} : 16'bz;  // Controlled_Buffer controlled_buffer_1

  // Other names for the same wires on the sheet: IR_L_O = IR_OUT
endmodule

module timing_control (
  input  TC_RST,
  input  CLK,
  output [4:0] T_OUT
);

  Counter #(.max('h1f), .width(5)) counter_1 (
    .clr(TC_RST), .load(1'b0), .up(1'b1), .count(1'b1), .clk(CLK), .Q(T_OUT));  // open: D, carry
endmodule

module memory_registers (
  input  CLK,
  input  RST,
  input  [15:0] D_BUS,
  input  MAR_WR_EN,
  input  [15:0] MEM_DATA_IN,
  input  MDR_WR_EN,
  input  MEM_sel,
  input  WR_sel,
  input  MDR_OUT_EN,
  output [15:0] MEM_ADDRESS_OUT,
  output [15:0] D_BUS_OUT,
  output [15:0] MEM_DATA_OUT,
  output RAM_WR_EN
);

  wire and_1_out, and_2_out, and_3_out, not_1_out, not_2_out;
  wire [15:0] controlled_buffer_1_out, MDR_q;

  assign controlled_buffer_1_out = not_1_out ? D_BUS : 16'bz;  // Controlled_Buffer controlled_buffer_1
  Register #(.width(16)) MAR (.D(D_BUS), .en(MAR_WR_EN), .clk(CLK), .Q(MEM_ADDRESS_OUT), .clr(RST));
  not not_1 (not_1_out, MEM_sel);
  assign controlled_buffer_1_out = and_1_out ? MEM_DATA_IN : 16'bz;  // Controlled_Buffer controlled_buffer_2
  Register #(.width(16)) MDR (.D(controlled_buffer_1_out), .en(MDR_WR_EN), .clk(CLK), .Q(MDR_q), .clr(RST));
  not not_2 (not_2_out, WR_sel);
  and and_1 (and_1_out, MEM_sel, not_2_out);
  assign MEM_DATA_OUT = and_2_out ? MDR_q : 16'bz;  // Controlled_Buffer controlled_buffer_3
  and and_2 (and_2_out, WR_sel, MDR_OUT_EN);
  and and_3 (and_3_out, not_1_out, MDR_OUT_EN);
  assign D_BUS_OUT = and_3_out ? MDR_q : 16'bz;  // Controlled_Buffer controlled_buffer_4

  assign RAM_WR_EN = WR_sel;
endmodule

module program_counter (
  input  CLK,
  input  RST,
  input  PC_OUT,
  input  PC_IN,
  input  PC_INC,
  input  [15:0] D_BUS,
  output [15:0] D_BUS_OUT
);

  wire [15:0] counter_1_q;

  Counter #(.max('hffff), .width(16)) counter_1 (
    .clr(RST), .load(PC_IN), .up(1'b1), .count(PC_INC), .clk(CLK), .D(D_BUS), .Q(counter_1_q));  // open: carry
  assign D_BUS_OUT = PC_OUT ? counter_1_q : 16'bz;  // Controlled_Buffer controlled_buffer_1
endmodule

module alu (
  input  CLK,
  input  RST,
  input  [15:0] D_BUS,
  input  X_IN,
  input  ADD_CARRY,
  input  [2:0] ALU_MUX,
  input  [3:0] FL_IN_ONZC,
  input  Y_IN,
  input  Y_OUT,
  output [3:0] FL_OUT,
  output [15:0] D_BUS_OUT
);

  wire and_2_out, C_OUT;
  wire [15:0] multiplexer_1_out, undriven, X1, Y_ADD, Y_AND, Y_EQ_B, Y_NOT, Y_OR, Y_REG_q, Y_SHRA, Y_SHRC,
       Y_SUB, Y_XOR;

  Register #(.width(16)) X_REG (.D(D_BUS), .en(X_IN), .clk(CLK), .Q(X1), .clr(RST));
  // Probe on Y_AND
  assign Y_AND = D_BUS & X1;  // AND_Gate and_1, 16 bits wide
  // Probe on Y_XOR
  assign Y_XOR = D_BUS ^ X1;  // XOR_Gate xor_1, 16 bits wide
  // Probe on Y_OR
  assign Y_OR = D_BUS | X1;  // OR_Gate or_1, 16 bits wide
  // Probe on Y_SUB
  Subtractor #(.width(16)) subtractor_1 (.a(D_BUS), .b(X1), .out(Y_SUB));  // open: bin, bout
  and and_2 (and_2_out, ADD_CARRY, FL_IN_ONZC[0]);
  // Probe on Y_ADD
  Adder #(.width(16)) adder_1 (.a(D_BUS), .b(X1), .out(Y_ADD), .cin(and_2_out), .cout(C_OUT));
  Multiplexer #(.select(3), .width(16)) multiplexer_1 (
    .in0(Y_ADD), .in1(Y_SUB), .in2(Y_AND), .in3(Y_OR), .in4(Y_XOR), .in5(Y_NOT), .in6(Y_EQ_B),
    .in7(undriven), .out(multiplexer_1_out));  // open: sel
  // Probe on Y_SHRA
  Shifter #(.shift("lr"), .width(16)) shifter_1 (.in(D_BUS), .\dist (4'b0001), .out(Y_SHRA));
  // Probe on Y_SHRC
  Shifter #(.shift("rr"), .width(16)) shifter_2 (.in(D_BUS), .\dist (4'b0001), .out(Y_SHRC));
  assign D_BUS_OUT = Y_OUT ? Y_REG_q : 16'bz;  // Controlled_Buffer controlled_buffer_1
  Register #(.width(16)) Y_REG (.D(multiplexer_1_out), .en(Y_IN), .clk(CLK), .Q(Y_REG_q), .clr(RST));

  // Other names for the same wires on the sheet: C_FLAG = FL_IN_ONZC[0]; Z_FLAG = FL_IN_ONZC[1];
  //   N_FLAG = FL_IN_ONZC[2]; O_FLAG = FL_IN_ONZC[3]; X2[15:0] = D_BUS
endmodule

module shift_control (
  input  CLK,
  input  RST,
  input  IR_OUT,
  input  SHC_IN,
  input  SHC_DEC,
  input  [15:0] in_6,
  output SHC_EQ0
);

  wire [3:0] counter_1_q;

  // Probe on in_6[3:0]
  Counter #(.max('hf), .width(4)) counter_1 (
    .clr(RST), .load(SHC_IN), .up(1'b0), .count(SHC_DEC), .clk(CLK), .D(in_6[3:0]), .Q(counter_1_q));  // open: carry
  nor nor_1 (SHC_EQ0, counter_1_q[3], counter_1_q[2], counter_1_q[1], counter_1_q[0]);

  // Other names for the same wires on the sheet: IR_L_O = IR_OUT
endmodule

module control_logic (
  input  [4:0] OPCODE,
  input  ADDRESSING_MODE,
  input  T_TIME
);
endmodule

module z74_alu (
  input  Y_OUT,
  input  Y_IN,
  input  RST,
  input  CLK,
  input  X_in,
  input  [3:0] S_in,
  input  M_in,
  input  Cin,
  input  [15:0] DATAIN,
  output [3:0] A_EQ_B,
  output C_out,
  output [15:0] Y_DATA_OUT
);

  wire A0, A1, A2, A3, A4, A5, A6, A7, A8, A9, A10, A11, A12, A13, A14, A15, F0, F1, F2, F3, F4, F5, F6, F7,
       F8, F9, F10, F11, F12, F13, F14, F15, n74181_2_p11, n74181_3_p11, n74181_4_p11, X_GB, Y_GB, Y_MN;

  not not_1 (Y_MN, Y_OUT);
  not not_2 (Y_GB, Y_IN);
  not not_3 (X_GB, X_in);
  ttl74173 X0 (
    .D1(DATAIN[0]), .D2(DATAIN[1]), .D3(DATAIN[2]), .D4(DATAIN[3]), .CLK(CLK), .RST(RST), .G1(X_GB),
    .G2(X_GB), .M(1'b0), .N(1'b0), .Q1(A0), .Q2(A1), .Q3(A2), .Q4(A3));
  ttl74173 X1 (
    .D1(DATAIN[4]), .D2(DATAIN[5]), .D3(DATAIN[6]), .D4(DATAIN[7]), .CLK(CLK), .RST(RST), .G1(X_GB),
    .G2(X_GB), .M(1'b0), .N(1'b0), .Q1(A4), .Q2(A5), .Q3(A6), .Q4(A7));
  ttl74173 X2 (
    .D1(DATAIN[8]), .D2(DATAIN[9]), .D3(DATAIN[10]), .D4(DATAIN[11]), .CLK(CLK), .RST(RST), .G1(X_GB),
    .G2(X_GB), .M(1'b0), .N(1'b0), .Q1(A8), .Q2(A9), .Q3(A10), .Q4(A11));
  ttl74173 X3 (
    .D1(DATAIN[12]), .D2(DATAIN[13]), .D3(DATAIN[14]), .D4(DATAIN[15]), .CLK(CLK), .RST(RST), .G1(X_GB),
    .G2(X_GB), .M(1'b0), .N(1'b0), .Q1(A12), .Q2(A13), .Q3(A14), .Q4(A15));
  Hex_Digit_Display hex_digit_display_1 (.value({A15, A14, A13, A12}));  // open: dp
  Hex_Digit_Display hex_digit_display_2 (.value({A7, A6, A5, A4}));  // open: dp
  Hex_Digit_Display #(.decimalPoint("false")) hex_digit_display_3 (.value({A11, A10, A9, A8}));
  Hex_Digit_Display hex_digit_display_4 (.value({A3, A2, A1, A0}));  // open: dp
  Hex_Digit_Display hex_digit_display_5 (.value({F15, F14, F13, F12}));  // open: dp
  Hex_Digit_Display #(.decimalPoint("false")) hex_digit_display_6 (.value({F11, F10, F9, F8}));
  Hex_Digit_Display hex_digit_display_7 (.value({F7, F6, F5, F4}));  // open: dp
  Hex_Digit_Display hex_digit_display_8 (.value({F3, F2, F1, F0}));  // open: dp
  // _74181 #(.ShowInternalStructure("true")) 74181_1: pin names not known; wires that end beside it: DATAIN[0], A0, S_in[3], S_in[2], S_in[1], S_in[0], Cin, A1, DATAIN[1], A2, DATAIN[2], A3, DATAIN[3]
  // _74181 #(.ShowInternalStructure("true")) 74181_2: pin names not known; wires that end beside it: M_in, F0, F1, F2, DATAIN[4], A4, S_in[3], S_in[2], S_in[1], S_in[0], n74181_2_p11, n74181_2_p11, A_EQ_B[3], F3, A5, DATAIN[5], A6, DATAIN[6], A7, DATAIN[7]
  // _74181 #(.ShowInternalStructure("true")) 74181_3: pin names not known; wires that end beside it: M_in, F4, F5, F6, DATAIN[8], A8, S_in[3], S_in[2], S_in[1], S_in[0], n74181_3_p11, n74181_3_p11, A_EQ_B[2], F7, A9, DATAIN[9], A10, DATAIN[10], A11, DATAIN[11]
  // _74181 #(.ShowInternalStructure("true")) 74181_4: pin names not known; wires that end beside it: M_in, F8, F9, F10, DATAIN[12], A12, S_in[3], S_in[2], S_in[1], S_in[0], n74181_4_p11, M_in, F12, F13, F14, n74181_4_p11, A_EQ_B[1], F11, A13, DATAIN[13], A14, DATAIN[14], A15, DATAIN[15], C_out, A_EQ_B[0], F15
  ttl74173 ttl74173_1 (
    .D1(F0), .D2(F1), .D3(F2), .D4(F3), .CLK(CLK), .RST(RST), .G1(Y_GB), .G2(Y_GB), .M(Y_MN), .N(Y_MN),
    .Q1(Y_DATA_OUT[0]), .Q2(Y_DATA_OUT[1]), .Q3(Y_DATA_OUT[2]), .Q4(Y_DATA_OUT[3]));
  ttl74173 ttl74173_2 (
    .D1(F4), .D2(F5), .D3(F6), .D4(F7), .CLK(CLK), .RST(RST), .G1(Y_GB), .G2(Y_GB), .M(Y_MN), .N(Y_MN),
    .Q1(Y_DATA_OUT[4]), .Q2(Y_DATA_OUT[5]), .Q3(Y_DATA_OUT[6]), .Q4(Y_DATA_OUT[7]));
  ttl74173 ttl74173_3 (
    .D1(F8), .D2(F9), .D3(F10), .D4(F11), .CLK(CLK), .RST(RST), .G1(Y_GB), .G2(Y_GB), .M(Y_MN), .N(Y_MN),
    .Q1(Y_DATA_OUT[8]), .Q2(Y_DATA_OUT[9]), .Q3(Y_DATA_OUT[10]), .Q4(Y_DATA_OUT[11]));
  ttl74173 ttl74173_4 (
    .D1(F12), .D2(F13), .D3(F14), .D4(F15), .CLK(CLK), .RST(RST), .G1(Y_GB), .G2(Y_GB), .M(Y_MN), .N(Y_MN),
    .Q1(Y_DATA_OUT[12]), .Q2(Y_DATA_OUT[13]), .Q3(Y_DATA_OUT[14]), .Q4(Y_DATA_OUT[15]));

  // Other names for the same wires on the sheet: A_EQ_B_4 = A_EQ_B[0]; A_EQ_B_3 = A_EQ_B[1]; A_EQ_B_2 = A_EQ_B[2];
  //   A_EQ_B_1 = A_EQ_B[3]; C_in = Cin; B0 = DATAIN[0]; X1 = DATAIN[0]; B1 = DATAIN[1]; X2 = DATAIN[1];
  //   B2 = DATAIN[2]; X3 = DATAIN[2]; B3 = DATAIN[3]; X4 = DATAIN[3]; B4 = DATAIN[4]; X5 = DATAIN[4]; B5 = DATAIN[5];
  //   X6 = DATAIN[5]; B6 = DATAIN[6]; X7 = DATAIN[6]; B7 = DATAIN[7]; X8 = DATAIN[7]; B8 = DATAIN[8]; X9 = DATAIN[8];
  //   B9 = DATAIN[9]; X10 = DATAIN[9]; B10 = DATAIN[10]; X11 = DATAIN[10]; B11 = DATAIN[11]; X12 = DATAIN[11];
  //   B12 = DATAIN[12]; X13 = DATAIN[12]; B13 = DATAIN[13]; X14 = DATAIN[13]; B14 = DATAIN[14]; X15 = DATAIN[14];
  //   B15 = DATAIN[15]; X16 = DATAIN[15]; Y_O_1 = Y_DATA_OUT[0]; Y_O_2 = Y_DATA_OUT[1]; Y_O_3 = Y_DATA_OUT[2];
  //   Y_O_4 = Y_DATA_OUT[3]; Y_O_5 = Y_DATA_OUT[4]; Y_O_6 = Y_DATA_OUT[5]; Y_O_7 = Y_DATA_OUT[6];
  //   Y_O_8 = Y_DATA_OUT[7]; Y_O_9 = Y_DATA_OUT[8]; Y_O_10 = Y_DATA_OUT[9]; Y_O_11 = Y_DATA_OUT[10];
  //   Y_O_12 = Y_DATA_OUT[11]; Y_O_13 = Y_DATA_OUT[12]; Y_O_14 = Y_DATA_OUT[13]; Y_O_15 = Y_DATA_OUT[14];
  //   Y_O_16 = Y_DATA_OUT[15]
endmodule

module ttl74173 (
  input  M,
  input  N,
  input  G1,
  input  G2,
  input  CLK,
  input  RST,
  input  D1,
  input  D2,
  input  D3,
  input  D4,
  output Q1,
  output Q2,
  output Q3,
  output Q4
);

  wire and_3_out, and_4_out, and_5_out, and_6_out, and_7_out, and_8_out, and_9_out, and_10_out, d_ff_1_q,
       d_ff_1_qn, d_ff_2_q, d_ff_2_qn, d_ff_3_q, d_ff_3_qn, d_ff_4_q, d_ff_4_qn, G12_AND, G12_NOT, MN_AND,
       not_1_out, not_2_out, not_3_out, not_4_out, not_6_out, not_7_out, not_8_out, not_9_out, or_1_out,
       or_2_out, or_3_out, or_4_out;

  not not_1 (not_1_out, G1);
  not not_2 (not_2_out, G2);
  not not_3 (not_3_out, M);
  not not_4 (not_4_out, N);
  and and_1 (G12_AND, not_1_out, not_2_out);
  not not_5 (G12_NOT, G12_AND);
  and and_2 (MN_AND, not_3_out, not_4_out);
  and and_3 (and_3_out, d_ff_1_q, G12_NOT);
  or or_1 (or_1_out, and_3_out, and_4_out);
  and and_4 (and_4_out, G12_AND, D1);
  and and_5 (and_5_out, d_ff_2_q, G12_NOT);
  or or_2 (or_2_out, and_5_out, and_6_out);
  and and_6 (and_6_out, G12_AND, D2);
  and and_7 (and_7_out, d_ff_3_q, G12_NOT);
  or or_3 (or_3_out, and_7_out, and_8_out);
  and and_8 (and_8_out, G12_AND, D3);
  and and_9 (and_9_out, d_ff_4_q, G12_NOT);
  or or_4 (or_4_out, and_9_out, and_10_out);
  and and_10 (and_10_out, G12_AND, D4);
  D_Flip_Flop d_ff_1 (.D(or_1_out), .clk(CLK), .Q(d_ff_1_q), .Qn(d_ff_1_qn), .reset(RST));  // open: preset
  D_Flip_Flop d_ff_2 (.D(or_2_out), .clk(CLK), .Q(d_ff_2_q), .Qn(d_ff_2_qn), .reset(RST));  // open: preset
  D_Flip_Flop d_ff_3 (.D(or_3_out), .clk(CLK), .Q(d_ff_3_q), .Qn(d_ff_3_qn), .reset(RST));  // open: preset
  D_Flip_Flop d_ff_4 (.D(or_4_out), .clk(CLK), .Q(d_ff_4_q), .Qn(d_ff_4_qn), .reset(RST));  // open: preset
  not not_6 (not_6_out, d_ff_1_qn);
  not not_7 (not_7_out, d_ff_2_qn);
  not not_8 (not_8_out, d_ff_3_qn);
  not not_9 (not_9_out, d_ff_4_qn);
  assign Q1 = MN_AND ? not_6_out : 1'bz;  // Controlled_Buffer controlled_buffer_1
  assign Q2 = MN_AND ? not_7_out : 1'bz;  // Controlled_Buffer controlled_buffer_2
  assign Q3 = MN_AND ? not_8_out : 1'bz;  // Controlled_Buffer controlled_buffer_3
  assign Q4 = MN_AND ? not_9_out : 1'bz;  // Controlled_Buffer controlled_buffer_4
endmodule
